// Logisim project vpu.circ as structural Verilog: 5 circuits, main circuit VPU
module VPU (
  input  in_1,
  input  [5:0] in_2,
  input  [4:0] in_3,
  input  [4:0] in_4,
  input  [31:0] in_5,
  input  [31:0] in_6,
  input  [23:0] in_7,
  output [31:0] VRegOutHi,
  output [31:0] VRegOutLo,
  output VBus32,
  output VBus64,
  output VPUError
);

  VReg VReg ();  // open: in_1, RAMOutHi, RAMOutLo, VSel1, WEn, out_8, out_10, out_7, out_9, VSel2
  VRegCtrl VRegCtrl ();  // open: vop, _16bitRegs, vlen, cfg

  assign VBus32 = 1'b0;
  assign VBus64 = 1'b0;
  assign VPUError = 1'b0;

  // Other names for the same wires on the sheet: CLK = in_1; RAMOutHi[31:0] = in_5; RAMOutLo[31:0] = in_6;
  //   RegOut2[23:0] = in_7; vop[5:0] = in_2; vrd[4:0] = in_3; vrs[4:0] = in_4
endmodule

module VRegRow (
  input  [31:0] RAMOutHi,
  input  [31:0] RAMOutLo,
  input  clk,
  input  [3:0] WVReg,
  input  RowEn,
  output [31:0] OutHi,
  output [31:0] OutLo
);

  wire [3:0] multiplexer_1_out, RegEn;

  Register register_1 (.D(RAMOutHi[31:24]), .en(RegEn[3]), .Q(OutHi[31:24]), .clk(clk));  // open: clr
  Register register_2 (.D(RAMOutHi[23:16]), .en(RegEn[3]), .Q(OutHi[23:16]), .clk(clk));  // open: clr
  Register register_3 (.D(RAMOutHi[15:8]), .en(RegEn[2]), .Q(OutHi[15:8]), .clk(clk));  // open: clr
  Register register_4 (.D(RAMOutHi[7:0]), .en(RegEn[2]), .Q(OutHi[7:0]), .clk(clk));  // open: clr
  Register register_5 (.D(RAMOutLo[31:24]), .en(RegEn[1]), .Q(OutLo[31:24]), .clk(clk));  // open: clr
  Register register_6 (.D(RAMOutLo[23:16]), .en(RegEn[1]), .Q(OutLo[23:16]), .clk(clk));  // open: clr
  Multiplexer #(.width(4), .enable("false")) multiplexer_1 (
    .in0(4'b0000), .in1(4'b1111), .out(multiplexer_1_out), .sel(RowEn));
  Register register_7 (.D(RAMOutLo[15:8]), .en(RegEn[0]), .Q(OutLo[15:8]), .clk(clk));  // open: clr
  assign RegEn = WVReg & multiplexer_1_out;  // AND_Gate and_1, 4 bits wide
  Register register_8 (.D(RAMOutLo[7:0]), .en(RegEn[0]), .Q(OutLo[7:0]), .clk(clk));  // open: clr

  // Other names for the same wires on the sheet: hi[31:0] = RAMOutHi; lo[31:0] = RAMOutLo
endmodule

module VReg (
  input  in_1,
  input  [31:0] RAMOutHi,
  input  [31:0] RAMOutLo,
  input  [7:0] VSel1,
  input  [7:0] VSel2,
  input  WEn,
  output [31:0] out_7,
  output [31:0] out_8,
  output [31:0] out_9,
  output [31:0] out_10
);

  wire demultiplexer_1_out0, demultiplexer_1_out1, demultiplexer_1_out2, demultiplexer_1_out3,
       demultiplexer_1_out4, demultiplexer_1_out5, demultiplexer_1_out6, demultiplexer_1_out7,
       demultiplexer_2_out0, demultiplexer_2_out1, demultiplexer_2_out2, demultiplexer_2_out3,
       demultiplexer_2_out4, demultiplexer_2_out5, demultiplexer_2_out6, demultiplexer_2_out7, not_1_out;
  wire [31:0] r00H, r00L, r01H, r01L, r02H, r02L, r03H, r03L, r04H, r04L, r05H, r05L, r06H, r06L, r07H, r07L,
       r08H, r08L, r09H, r09L, r10H, r10L, r11H, r11L, r12H, r12L, r13H, r13L, r14H, r14L, r15H, r15L;

  VRegRow vregrow_1 (
    .clk(in_1), .RAMOutHi(RAMOutHi), .RAMOutLo(RAMOutLo), .OutHi(r00H), .OutLo(r00L), .WVReg(VSel1[3:0]),
    .RowEn(demultiplexer_1_out0));
  VRegRow vregrow_2 (
    .clk(in_1), .RAMOutHi(RAMOutHi), .RAMOutLo(RAMOutLo), .OutHi(r01H), .OutLo(r01L), .WVReg(VSel1[3:0]),
    .RowEn(demultiplexer_1_out1));
  VRegRow vregrow_3 (
    .clk(in_1), .RAMOutHi(RAMOutHi), .RAMOutLo(RAMOutLo), .OutHi(r02H), .OutLo(r02L), .WVReg(VSel1[3:0]),
    .RowEn(demultiplexer_1_out2));
  VRegRow vregrow_4 (
    .clk(in_1), .RAMOutHi(RAMOutHi), .RAMOutLo(RAMOutLo), .OutHi(r03H), .OutLo(r03L), .WVReg(VSel1[3:0]),
    .RowEn(demultiplexer_1_out3));
  VRegRow vregrow_5 (
    .clk(in_1), .RAMOutHi(RAMOutHi), .RAMOutLo(RAMOutLo), .OutHi(r04H), .OutLo(r04L), .WVReg(VSel1[3:0]),
    .RowEn(demultiplexer_1_out4));
  VRegRow vregrow_6 (
    .clk(in_1), .RAMOutHi(RAMOutHi), .RAMOutLo(RAMOutLo), .OutHi(r05H), .OutLo(r05L), .WVReg(VSel1[3:0]),
    .RowEn(demultiplexer_1_out5));
  VRegRow vregrow_7 (
    .clk(in_1), .RAMOutHi(RAMOutHi), .RAMOutLo(RAMOutLo), .OutHi(r06H), .OutLo(r06L), .WVReg(VSel1[3:0]),
    .RowEn(demultiplexer_1_out6));
  VRegRow vregrow_8 (
    .clk(in_1), .RAMOutHi(RAMOutHi), .RAMOutLo(RAMOutLo), .OutHi(r07H), .OutLo(r07L), .WVReg(VSel1[3:0]),
    .RowEn(demultiplexer_1_out7));
  Demultiplexer #(.select(3)) demultiplexer_1 (
    .out0(demultiplexer_1_out0), .out1(demultiplexer_1_out1), .out2(demultiplexer_1_out2),
    .out3(demultiplexer_1_out3), .out4(demultiplexer_1_out4), .out5(demultiplexer_1_out5),
    .out6(demultiplexer_1_out6), .out7(demultiplexer_1_out7), .in(WEn), .sel(VSel1[6:4]), .en(not_1_out));
  not not_1 (not_1_out, VSel1[7]);
  VRegRow vregrow_9 (
    .clk(in_1), .RAMOutHi(RAMOutHi), .RAMOutLo(RAMOutLo), .OutHi(r08H), .OutLo(r08L), .WVReg(VSel1[3:0]),
    .RowEn(demultiplexer_2_out0));
  VRegRow vregrow_10 (
    .clk(in_1), .RAMOutHi(RAMOutHi), .RAMOutLo(RAMOutLo), .OutHi(r09H), .OutLo(r09L), .WVReg(VSel1[3:0]),
    .RowEn(demultiplexer_2_out1));
  VRegRow vregrow_11 (
    .clk(in_1), .RAMOutHi(RAMOutHi), .RAMOutLo(RAMOutLo), .OutHi(r10H), .OutLo(r10L), .WVReg(VSel1[3:0]),
    .RowEn(demultiplexer_2_out2));
  VRegRow vregrow_12 (
    .clk(in_1), .RAMOutHi(RAMOutHi), .RAMOutLo(RAMOutLo), .OutHi(r11H), .OutLo(r11L), .WVReg(VSel1[3:0]),
    .RowEn(demultiplexer_2_out3));
  VRegRow vregrow_13 (
    .clk(in_1), .RAMOutHi(RAMOutHi), .RAMOutLo(RAMOutLo), .OutHi(r12H), .OutLo(r12L), .WVReg(VSel1[3:0]),
    .RowEn(demultiplexer_2_out4));
  VRegRow vregrow_14 (
    .clk(in_1), .RAMOutHi(RAMOutHi), .RAMOutLo(RAMOutLo), .OutHi(r13H), .OutLo(r13L), .WVReg(VSel1[3:0]),
    .RowEn(demultiplexer_2_out5));
  VRegRow vregrow_15 (
    .clk(in_1), .RAMOutHi(RAMOutHi), .RAMOutLo(RAMOutLo), .OutHi(r14H), .OutLo(r14L), .WVReg(VSel1[3:0]),
    .RowEn(demultiplexer_2_out6));
  VRegRow vregrow_16 (
    .clk(in_1), .RAMOutHi(RAMOutHi), .RAMOutLo(RAMOutLo), .OutHi(r15H), .OutLo(r15L), .WVReg(VSel1[3:0]),
    .RowEn(demultiplexer_2_out7));
  Demultiplexer #(.select(3)) demultiplexer_2 (
    .out0(demultiplexer_2_out0), .out1(demultiplexer_2_out1), .out2(demultiplexer_2_out2),
    .out3(demultiplexer_2_out3), .out4(demultiplexer_2_out4), .out5(demultiplexer_2_out5),
    .out6(demultiplexer_2_out6), .out7(demultiplexer_2_out7), .in(WEn), .sel(VSel1[6:4]), .en(VSel1[7]));
  Multiplexer #(.select(4), .width(32), .enable("false")) multiplexer_1 (
    .in0(r00H), .in1(r01H), .in2(r02H), .in3(r03H), .in4(r04H), .in5(r05H), .in6(r06H), .in7(r07H),
    .in8(r08H), .in9(r09H), .in10(r10H), .in11(r11H), .in12(r12H), .in13(r13H), .in14(r14H), .in15(r15H),
    .out(out_7), .sel(VSel1[7:4]));
  Multiplexer #(.select(4), .width(32), .enable("false")) multiplexer_2 (
    .in0(r00L), .in1(r01L), .in2(r02L), .in3(r03L), .in4(r04L), .in5(r05L), .in6(r06L), .in7(r07L),
    .in8(r08L), .in9(r09L), .in10(r10L), .in11(r11L), .in12(r12L), .in13(r13L), .in14(r14L), .in15(r15L),
    .out(out_9), .sel(VSel1[7:4]));
  Multiplexer #(.select(4), .width(32), .enable("false")) multiplexer_3 (
    .in0(r00H), .in1(r01H), .in2(r02H), .in3(r03H), .in4(r04H), .in5(r05H), .in6(r06H), .in7(r07H),
    .in8(r08H), .in9(r09H), .in10(r10H), .in11(r11H), .in12(r12H), .in13(r13H), .in14(r14H), .in15(r15H),
    .out(out_8), .sel(VSel2[7:4]));
  Multiplexer #(.select(4), .width(32), .enable("false")) multiplexer_4 (
    .in0(r00L), .in1(r01L), .in2(r02L), .in3(r03L), .in4(r04L), .in5(r05L), .in6(r06L), .in7(r07L),
    .in8(r08L), .in9(r09L), .in10(r10L), .in11(r11L), .in12(r12L), .in13(r13L), .in14(r14L), .in15(r15L),
    .out(out_10), .sel(VSel2[7:4]));

  // Other names for the same wires on the sheet: clk = in_1; RAMhi[31:0] = RAMOutHi; RAMlo[31:0] = RAMOutLo;
  //   rOutHi1[31:0] = out_7; rOutHi2[31:0] = out_8; rOutLo1[31:0] = out_9; rOutLo2[31:0] = out_10;
  //   RegSel1[3:0] = VSel1[3:0]; RowSel1[3:0] = VSel1[7:4]; RegSel2[3:0] = VSel2[3:0]; RowSel2[3:0] = VSel2[7:4]
endmodule

module VRegCtrl (
  input  [5:0] vop,
  output [3:0] _16bitRegs,
  output vlen,
  output cfg
);
endmodule

module VTC (
  input  [2:0] vlen,
  input  [3:0] num16,
  input  [5:0] VirtAddr,
  output [7:0] out_4
);

  wire comparator_1_lt, not_1_out;
  wire [1:0] priority_encoder_1_out;
  wire [2:0] lgvlen;
  wire [7:0] adder_1_out, bit_extender_1_out, shifter_1_out, shifter_2_out, shifter_3_out, vaddr;

  Priority_Encoder #(.select(2), .disabled(0)) priority_encoder_1 (
    .in0(vlen[0]), .in1(vlen[1]), .in2(vlen[2]), .out(priority_encoder_1_out));  // open: in3, gs, en_out, en_in
  assign bit_extender_1_out = {{4{1'b0}}, num16};  // Bit_Extender bit_extender_1
  assign lgvlen = {{1{1'b0}}, priority_encoder_1_out};  // Bit_Extender bit_extender_2
  assign vaddr = {{2{1'b0}}, VirtAddr};  // Bit_Extender bit_extender_3
  Adder adder_1 (.a(bit_extender_1_out), .b(vaddr), .out(adder_1_out));  // open: cin, cout
  Comparator comparator_1 (.a(vaddr), .b(bit_extender_1_out), .lt(comparator_1_lt));  // open: gt, eq
  not not_1 (not_1_out, comparator_1_lt);
  Shifter shifter_1 (.in(vaddr), .\dist (lgvlen), .out(shifter_1_out));
  Shifter shifter_2 (.in(shifter_1_out), .\dist (3'b001), .out(shifter_2_out));
  Multiplexer #(.width(8), .enable("false")) multiplexer_1 (
    .in0(shifter_2_out), .in1(shifter_3_out), .out(out_4), .sel(not_1_out));
  Shifter shifter_3 (.in(adder_1_out), .\dist (lgvlen), .out(shifter_3_out));
  // Probe on out_4
endmodule
